# Fritzing sketch police-project-led (saved by Fritzing 0.9.3b)
breadboards: 1

parts:
  LED1 = LED - 5mm [color="Red (633nm)" package="5 mm [THT]"]
  LED2 = LED - 5mm [color="Red (633nm)" package="5 mm [THT]"]
  LED3 = LED - 5mm [color="Red (633nm)" package="5 mm [THT]"]
  LED4 = LED - 5mm [color="Red (633nm)" package="5 mm [THT]"]
  LED5 = LED - 5mm [color="Red (633nm)" package="5 mm [THT]"]
  Part2 = PWM Shield
  R1 = Resistor [tolerance=±5% resistance=220 package=THT]
  R2 = Resistor [tolerance=±5% resistance=220 package=THT]
  R3 = Resistor [tolerance=±5% resistance=220 package=THT]
  R4 = Resistor [tolerance=±5% resistance=220 package=THT]
  R5 = Resistor [tolerance=±5% resistance=220 package=THT]
  R6 = Resistor [tolerance=±5% resistance=220 package=THT]
  R7 = Resistor [tolerance=±5% resistance=220 package=THT]
  R8 = Resistor [tolerance=±5% resistance=220 package=THT]
  R9 = Resistor [tolerance=±5% resistance=220 package=THT]
  R10 = Resistor [tolerance=±5% resistance=220 package=THT]
  LED6 = LED - 5mm [color="Red (633nm)" package="5 mm [THT]"]
  LED7 = LED - 5mm [color="Red (633nm)" package="5 mm [THT]"]
  LED8 = LED - 5mm [color="Red (633nm)" package="5 mm [THT]"]
  LED9 = LED - 5mm [color="Red (633nm)" package="5 mm [THT]"]
  LED10 = LED - 5mm [color="Red (633nm)" package="5 mm [THT]"]
  S1 = Pushbutton [package="[THT]"]
  S2 = Pushbutton [package="[THT]"]

nets:
  N1: LED1.cathode, LED2.cathode, LED3.cathode, LED4.cathode, LED5.cathode, Part2.GND, Part2.GND_-_GND@0, LED6.cathode, LED7.cathode, LED8.cathode, LED9.cathode, LED10.cathode, S1.Pin_3, S1.Pin_4, S2.Pin_3, S2.Pin_4
  N2: LED1.anode, R1.Pin_0
  N3: LED2.anode, R2.Pin_0
  N4: LED3.anode, R3.Pin_0
  N5: LED4.anode, R5.Pin_0
  N6: LED5.anode, R4.Pin_0
  N7: Part2.D2, S2.Pin_1, S2.Pin_2
  N8: Part2.GSCLK_-_D3, S1.Pin_1, S1.Pin_2
  N9: Part2.D4, R10.Pin_1
  N10: Part2.D5, R9.Pin_1
  N11: Part2.D6, R8.Pin_1
  N12: Part2.D7, R7.Pin_1
  N13: Part2.D8, R6.Pin_1
  N14: Part2.XLAT_-_D9, R5.Pin_1
  N15: Part2.BLANK_-_D10, R4.Pin_1
  N16: Part2.SIN_-_D11, R3.Pin_1
  N17: Part2.D12, R2.Pin_1
  N18: Part2.SCLK_-_D13, R1.Pin_1
  N19: R6.Pin_0, LED6.anode
  N20: R7.Pin_0, LED7.anode
  N21: R8.Pin_0, LED8.anode
  N22: R9.Pin_0, LED9.anode
  N23: R10.Pin_0, LED10.anode
